# Fritzing sketch scope_v2 (saved by Fritzing 0.9.3b)
circuit board: 8.46667cm x 5.64444cm

parts:
  RFID1 = ArduCam
  Part1 = Arduino Uno (Rev3)
  Zeiss_trigger_OUT = Power plug
  C1_100uF1 = Electrolytic Capacitor [capacitance=1µF package="100 mil [THT, electrolytic]"]
  M2 = Stepper Motor - Unipolar
  M3 = xy-mos d4184 [package=THT]
  MD09B1 = Pololu A4988 [package=SO16]
  LED1 = LEDs [package=led10mm]
  M4 = xy-mos d4184 [package=THT]
  Main_Power_12V = Power plug
  S1 = SWITCH-SPST-2 [package=switch-spst-vertical]
  Pololu_A1 = Pololu A4988 [package=SO16]
  4_7kΩ = Resistor [tolerance=±5% resistance=4.7k package="0402 [SMD]"]
  Peltiere = Peltier Element
  J2 = Power Jack [package=power_jack_slot]
  J3 = Power Plug
  M5 = Stepper Motor - Unipolar
  10k_NTC = Temperature Sensor (Thermistor) [thermistor_type=NTC package=THT]  # not connected
  Arduino_CNC_Shield_V3_00_1 = Arduino_CNC_V3.00
  Part2 = Arduino Uno (Rev3)  # not connected
  DRV_1 = Pololu DRV 8825 Stepper Motor Carrier, High Current [package=SO16]  # not connected
  Pololu_A2 = Pololu A4988 [package=SO16]  # not connected

nets (from the breadboard view):
  N1: RFID1.CS, Arduino_CNC_Shield_V3_00_1.End_Stops_Y+_(and_Y-)
  N2: RFID1.MOSI, Arduino_CNC_Shield_V3_00_1.End_Stops_Z+_(and_Z-)_/_SpnEn
  N3: RFID1.MISO, Arduino_CNC_Shield_V3_00_1.SpnEn_/_Z_Limit
  N4: RFID1.SCK, Arduino_CNC_Shield_V3_00_1.SpnDir
  VCC: RFID1.VCC, Arduino_CNC_Shield_V3_00_1.5V
  N5: RFID1.GND, Arduino_CNC_Shield_V3_00_1.CoolEn_(Gnd)
  N6: RFID1.SDA, Arduino_CNC_Shield_V3_00_1.SDA
  N7: RFID1.SCL, Arduino_CNC_Shield_V3_00_1.SCL_/_Probe
  N8: Part1.A1, Zeiss_trigger_OUT.VCC, 4_7kΩ.Pin_0
  N9: Part1.D8, Pololu_A1.DIR
  GND: Part1.D9_PWM, Part1.D6_PWM, C1_100uF1.-, C1_100uF1.+, M3.PWM, M3.GND#2, M3.+, MD09B1.GND#14, MD09B1.VMOT, LED1.A, M4.PWM, M4.GND#2, M4.+, Main_Power_12V.GND, S1.P, Pololu_A1.GND#14, Pololu_A1.VMOT, Peltiere.pin1, J2.GND, J2.tip_GND, J3.GND, J3.tip_GND
  GND_2: Part1.GND, Zeiss_trigger_OUT.GND, M3.GND#1, M3.LOAD, MD09B1.GND#8, LED1.C, M4.GND#1, M4.LOAD, Pololu_A1.GND#8, 4_7kΩ.Pin_1, J2.GNDBREAK
  N10: Part1.D3_PWM, Pololu_A1.STEP
  N11: Part1.D4, MD09B1.DIR
  N12: Part1.D5_PWM, MD09B1.STEP
  N13: Part1.D7, MD09B1.ENABLE, Pololu_A1.ENABLE
  VDD: Part1.5V, MD09B1.MS1, MD09B1.MS2, MD09B1.MS3, MD09B1.VDD, Pololu_A1.MS1, Pololu_A1.MS2, Pololu_A1.MS3, Pololu_A1.VDD
  N14: M2.A, MD09B1.2B
  N15: M2.C, MD09B1.2A
  N16: M2.B, MD09B1.1A
  N17: M2.D, MD09B1.1B
  N18: MD09B1.RESET, MD09B1.SLEEP
  N19: Main_Power_12V.VCC, S1.O
  N20: Pololu_A1.RESET, Pololu_A1.SLEEP
  N21: Pololu_A1.1B, M5.D
  N22: Pololu_A1.1A, M5.B
  N23: Pololu_A1.2A, M5.C
  N24: Pololu_A1.2B, M5.A
  N25: Peltiere.pin2, J2.PWR, J2.tip_PWR, J3.PWR, J3.tip_PWR
  N26: Arduino_CNC_Shield_V3_00_1.X_-_M2, Arduino_CNC_Shield_V3_00_1.X_-_M2_(5V)
  N27: Arduino_CNC_Shield_V3_00_1.Z_-_M2, Arduino_CNC_Shield_V3_00_1.Z_-_M2_(5V)

custom parts:
  ArduCam: 5 MINI plus
  xy-mos d4184: xy-mos d4184 Two parallel N-Channel logic compatible MOSFETS with low Rds(on) for high current low-side switching applications.
  Power Jack: Power Jack This is the standard 5.5mm barrel jack for power. Ths one is modified to mate with the barrel plug part and allow the two to "connect" so batteries and wall warts can be "connected" in breadboard and will go through to schematic.
  Power Plug: Power Jack This is the standard 5.5mm barrel plug for power. This part has bendable leads (i.e. wires in the real world) to connect to wall warts or the breadboard in the standard wire end, and hidden connectors on the tip end that will connect when "plugged in" (overlapped with the jack so it appears "plugged in" in breadboard) to the modified coax jack part. Internal busses connect the two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
  Arduino_CNC_V3.00: Protoneer Arduino CNC Shield V3.00 If using Grbl V0.9: The “A” axis can not be used (yet). The “SCL” (Arduino A5) pin is now used for 'Probing' input. The “End Stops Z+ & Z-” (Arduino D11) and “SpnEn” (Arduino D12) have been switched!
  Pololu DRV 8825 Stepper Motor Carrier, High Current: DRV 8825 This is a Stepper Motor Controller for integrated circuits. This breakout board for TI’s DRV8825 microstepping bipolar stepper motor driver features adjustable current limiting, over-current and over-temperature protection, and six microstep resolutions (down to 1/32-step). It operates from 8.2 V to 45 V and can deliver up to approximately 1.5 A per phase without a heat sink or forced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
